// Logisim project cpu.circ as structural Verilog: 7 circuits, main circuit CPU
module CPU (
  input  MC_E,
  input  MOV_E,
  input  R_EN,
  input  IS32,
  input  [15:0] INSTR
);

  wire ALU_RW, button_1_out, CIN, CLK, not_1_out, not_2_out, R_WE;
  wire [2:0] counter_1_q;
  wire [3:0] BLOCKA, MC_ADDR, MCADDR, R_AD;
  wire [31:0] ADDR_BUS, DATA_BUS, R_DB;

  assign ADDR_BUS = IS32 ? R_DB : 32'bz;  // Controlled_Buffer controlled_buffer_1
  not not_1 (not_1_out, IS32);
  assign DATA_BUS = not_1_out ? R_DB : 32'bz;  // Controlled_Buffer controlled_buffer_2
  assign R_DB = DATA_BUS;  // Buffer buffer_1, 32 bits wide
  Clock clock_1 (.out(CLK));
  REGS regs_1 (.ADDR(R_AD), .DATA_IN(R_DB), .DATA_OUT(R_DB), .ENA(R_EN), .CLK(CLK), .IS32(IS32), .WE(R_WE));
  ALU alu_1 (.OPCODE(INSTR[15:12]), .RW(CIN), .CLK(ALU_RW), .ENA(CLK));  // open: DATA_IN, DATA_OUT
  Button button_1 (.out(button_1_out));
  assign MCADDR = MOV_E ? BLOCKA : 4'bz;  // Controlled_Buffer controlled_buffer_3
  not not_2 (not_2_out, MOV_E);
  assign MCADDR = not_2_out ? INSTR[15:12] : 4'bz;  // Controlled_Buffer controlled_buffer_4
  Counter #(.width(3), .max('h7)) counter_1 (
    .count(button_1_out), .Q(counter_1_q), .clk(button_1_out));  // open: load, D, carry, clr
  ROM rom_1 (.addr({MOV_E, MC_ADDR, counter_1_q}), .sel(MC_E));  // open: data

  // Other names for the same wires on the sheet: EN32 = IS32; BLOCKC[3:0] = INSTR[3:0]; BLOCKB[3:0] = INSTR[7:4];
  //   OPCODE[3:0] = INSTR[15:12]

  // Notes on the sheet:
  //   MC_E: pull=down
  //   IS32: pull=down
  //   INSTR: pull=down
  //   R_EN: pull=down
  //   MOV_E: pull=down
endmodule

module REG32 (
  input  [1:0] ADDR,
  input  [31:0] DATA_IN,
  input  ENA,
  input  RW,
  input  IS32,
  input  CLK,
  output [31:0] DATA_OUT
);

  wire and_1_out, and_2_out, and_3_out, and_4_out, and_5_out, and_6_out, and_7_out, and_8_out, and_9_out,
       and_10_out, controlled_buffer_9_out, controlled_buffer_12_out, controlled_buffer_19_out,
       controlled_buffer_24_out, decoder_1_out0, decoder_1_out1, decoder_1_out2, decoder_1_out3, not_1_out;
  wire [7:0] controlled_buffer_5_out, controlled_buffer_10_out, controlled_buffer_15_out,
       controlled_buffer_20_out, LH_q, LL_q, UH_q, UL_q;
  wire [31:0] controlled_buffer_1_out, controlled_buffer_3_out, pull_resistor_1_node;

  Decoder #(.select(2), .enable("false")) decoder_1 (
    .out0(decoder_1_out0), .out1(decoder_1_out1), .out2(decoder_1_out2), .out3(decoder_1_out3), .sel(ADDR));
  Pull_Resistor pull_resistor_1 (.node(pull_resistor_1_node));
  assign controlled_buffer_1_out = not_1_out ? pull_resistor_1_node : 32'bz;  // Controlled_Buffer controlled_buffer_1
  assign DATA_OUT = ENA ? controlled_buffer_1_out : 32'bz;  // Controlled_Buffer controlled_buffer_2
  not not_1 (not_1_out, RW);
  assign controlled_buffer_3_out = ENA ? DATA_IN : 32'bz;  // Controlled_Buffer controlled_buffer_3
  assign pull_resistor_1_node = RW ? controlled_buffer_3_out : 32'bz;  // Controlled_Buffer controlled_buffer_4
  and and_1 (and_1_out, decoder_1_out3, ~IS32, RW);  // AND_Gate
  assign controlled_buffer_5_out = and_1_out ? pull_resistor_1_node[7:0] : 8'bz;  // Controlled_Buffer controlled_buffer_5
  assign pull_resistor_1_node[7:0] = and_4_out ? UH_q : 8'bz;  // Controlled_Buffer controlled_buffer_6
  Register UH (.D(controlled_buffer_5_out), .Q(UH_q), .clk(controlled_buffer_9_out));  // open: en, clr
  assign controlled_buffer_5_out = and_2_out ? pull_resistor_1_node[31:24] : 8'bz;  // Controlled_Buffer controlled_buffer_7
  and and_2 (and_2_out, RW, IS32);
  and and_3 (and_3_out, IS32, ~RW);  // AND_Gate
  assign pull_resistor_1_node[31:24] = and_3_out ? UH_q : 8'bz;  // Controlled_Buffer controlled_buffer_8
  assign controlled_buffer_9_out = ENA ? CLK : 1'bz;  // Controlled_Buffer controlled_buffer_9
  and and_4 (and_4_out, decoder_1_out3, ~IS32, ~RW);  // AND_Gate
  and and_5 (and_5_out, decoder_1_out2, ~IS32, RW);  // AND_Gate
  assign controlled_buffer_10_out = and_5_out ? pull_resistor_1_node[7:0] : 8'bz;  // Controlled_Buffer controlled_buffer_10
  assign controlled_buffer_10_out = and_2_out ? pull_resistor_1_node[23:16] : 8'bz;  // Controlled_Buffer controlled_buffer_11
  assign controlled_buffer_12_out = ENA ? CLK : 1'bz;  // Controlled_Buffer controlled_buffer_12
  assign pull_resistor_1_node[7:0] = and_6_out ? UL_q : 8'bz;  // Controlled_Buffer controlled_buffer_13
  and and_6 (and_6_out, decoder_1_out2, ~IS32, ~RW);  // AND_Gate
  Register UL (.D(controlled_buffer_10_out), .Q(UL_q), .clk(controlled_buffer_12_out));  // open: en, clr
  assign pull_resistor_1_node[23:16] = and_3_out ? UL_q : 8'bz;  // Controlled_Buffer controlled_buffer_14
  and and_7 (and_7_out, decoder_1_out1, ~IS32, RW);  // AND_Gate
  assign controlled_buffer_15_out = and_7_out ? pull_resistor_1_node[7:0] : 8'bz;  // Controlled_Buffer controlled_buffer_15
  assign controlled_buffer_15_out = and_2_out ? pull_resistor_1_node[15:8] : 8'bz;  // Controlled_Buffer controlled_buffer_16
  assign pull_resistor_1_node[7:0] = and_8_out ? LH_q : 8'bz;  // Controlled_Buffer controlled_buffer_17
  and and_8 (and_8_out, decoder_1_out1, ~IS32, ~RW);  // AND_Gate
  Register LH (.D(controlled_buffer_15_out), .Q(LH_q), .clk(controlled_buffer_19_out));  // open: en, clr
  assign pull_resistor_1_node[15:8] = and_3_out ? LH_q : 8'bz;  // Controlled_Buffer controlled_buffer_18
  assign controlled_buffer_19_out = ENA ? CLK : 1'bz;  // Controlled_Buffer controlled_buffer_19
  and and_9 (and_9_out, decoder_1_out0, ~IS32, RW);  // AND_Gate
  assign controlled_buffer_20_out = and_9_out ? pull_resistor_1_node[7:0] : 8'bz;  // Controlled_Buffer controlled_buffer_20
  assign pull_resistor_1_node[7:0] = and_10_out ? LL_q : 8'bz;  // Controlled_Buffer controlled_buffer_21
  and and_10 (and_10_out, decoder_1_out0, ~IS32, ~RW);  // AND_Gate
  Register LL (.D(controlled_buffer_20_out), .Q(LL_q), .clk(controlled_buffer_24_out));  // open: en, clr
  assign controlled_buffer_20_out = and_2_out ? pull_resistor_1_node[7:0] : 8'bz;  // Controlled_Buffer controlled_buffer_22
  assign pull_resistor_1_node[7:0] = and_3_out ? LL_q : 8'bz;  // Controlled_Buffer controlled_buffer_23
  assign controlled_buffer_24_out = ENA ? CLK : 1'bz;  // Controlled_Buffer controlled_buffer_24

  // Notes on the sheet:
  //   ENA: pull=down
  //   CLK: pull=down
  //   DATA_IN: pull=down
  //   DATA_OUT: pull=down
  //   ADDR: pull=down
  //   RW: pull=down
  //   IS32: pull=down
endmodule

module REGS (
  input  [3:0] ADDR,
  input  [31:0] DATA_IN,
  input  ENA,
  input  CLK,
  input  IS32,
  input  WE,
  output [31:0] DATA_OUT
);

  wire A_ENA, B_ENA, C_ENA, D_ENA, not_1_out;
  wire [31:0] controlled_buffer_1_out, controlled_buffer_2_out, DATA;

  REG32 reg32_1 (.ADDR(ADDR[3:2]), .DATA_OUT(DATA), .DATA_IN(DATA), .ENA(A_ENA), .RW(WE), .IS32(IS32), .CLK(CLK));
  assign controlled_buffer_1_out = ENA ? DATA_IN : 32'bz;  // Controlled_Buffer controlled_buffer_1
  assign controlled_buffer_2_out = not_1_out ? DATA : 32'bz;  // Controlled_Buffer controlled_buffer_2
  assign DATA_OUT = ENA ? controlled_buffer_2_out : 32'bz;  // Controlled_Buffer controlled_buffer_3
  not not_1 (not_1_out, WE);
  Decoder #(.select(2), .disabled(0)) decoder_1 (
    .out0(A_ENA), .out1(B_ENA), .out2(C_ENA), .out3(D_ENA), .sel(ADDR[1:0]), .en(ENA));
  REG32 reg32_2 (.ADDR(ADDR[3:2]), .DATA_OUT(DATA), .DATA_IN(DATA), .ENA(B_ENA), .RW(WE), .IS32(IS32), .CLK(CLK));
  assign DATA = WE ? controlled_buffer_1_out : 32'bz;  // Controlled_Buffer controlled_buffer_4
  REG32 reg32_3 (.ADDR(ADDR[3:2]), .DATA_OUT(DATA), .DATA_IN(DATA), .ENA(C_ENA), .RW(WE), .IS32(IS32), .CLK(CLK));
  REG32 reg32_4 (.ADDR(ADDR[3:2]), .DATA_OUT(DATA), .DATA_IN(DATA), .ENA(D_ENA), .RW(WE), .IS32(IS32), .CLK(CLK));

  // Other names for the same wires on the sheet: L_ADDR[1:0] = ADDR[1:0]; H_ADDR[1:0] = ADDR[3:2]

  // Notes on the sheet:
  //   ADDR: pull=down
  //   CLK: pull=down
  //   IS32: pull=down
  //   DATA_IN: pull=down
  //   DATA_OUT: pull=down
  //   ENA: pull=down
  //   WE: pull=down
endmodule

module ALU (
  input  [3:0] OPCODE,
  input  RW,
  input  CLK,
  input  ENA,
  input  [15:0] DATA_IN,
  output [7:0] DATA_OUT
);

  wire ADC, ADD, adder_1_cout, CARRY, CIN, controlled_buffer_1_out, COUT, LSC, LSH, lsh_1_cout, NAND, OE,
       or_1_out, or_2_out, or_3_out, or_4_out, or_5_out, or_6_out, RSC, RSH, rsh_1_cout, SBC, SUB,
       subtractor_1_bout, undriven, XOR;
  wire [7:0] adder_1_out, lsh_1_out, nand_1_out, rsh_1_out, subtractor_1_out, xor_1_out;
  wire [15:0] register_2_q;

  assign controlled_buffer_1_out = ENA ? RW : 1'bz;  // Controlled_Buffer controlled_buffer_1
  Register #(.width(1), .trigger("falling")) register_1 (
    .D(or_1_out), .en(undriven), .Q(CARRY), .clk(CLK));  // open: clr
  or or_1 (or_1_out, ADD, SUB, LSH, RSH, ADC, SBC, LSC, RSC);
  Pull_Resistor pull_resistor_1 (.node(CIN));
  assign CIN = or_2_out ? CARRY : 1'bz;  // Controlled_Buffer controlled_buffer_2
  or or_2 (or_2_out, ADC, SBC, LSC, RSC);
  Register #(.width(16)) register_2 (
    .D(DATA_IN), .en(controlled_buffer_1_out), .Q(register_2_q), .clk(CLK));  // open: clr
  or or_3 (or_3_out, ADD, ADC);
  assign DATA_OUT = or_3_out ? adder_1_out : 8'bz;  // Controlled_Buffer controlled_buffer_3
  Adder adder_1 (.a(register_2_q[7:0]), .b(register_2_q[15:8]), .out(adder_1_out), .cin(CIN), .cout(adder_1_cout));
  assign COUT = or_3_out ? adder_1_cout : 1'bz;  // Controlled_Buffer controlled_buffer_4
  or or_4 (or_4_out, SUB, SBC);
  assign DATA_OUT = or_4_out ? subtractor_1_out : 8'bz;  // Controlled_Buffer controlled_buffer_5
  Subtractor subtractor_1 (
    .a(register_2_q[7:0]), .b(register_2_q[15:8]), .out(subtractor_1_out), .bin(CIN), .bout(subtractor_1_bout));
  assign COUT = or_4_out ? subtractor_1_bout : 1'bz;  // Controlled_Buffer controlled_buffer_6
  or or_5 (or_5_out, LSH, LSC);
  LSH lsh_1 (.OUT(lsh_1_out), .IN(register_2_q[7:0]), .CIN(CIN), .COUT(lsh_1_cout));
  assign DATA_OUT = or_5_out ? lsh_1_out : 8'bz;  // Controlled_Buffer controlled_buffer_7
  assign COUT = or_5_out ? lsh_1_cout : 1'bz;  // Controlled_Buffer controlled_buffer_8
  or or_6 (or_6_out, RSH, RSC);
  RSH rsh_1 (.OUT(rsh_1_out), .COUT(rsh_1_cout), .CIN(CIN), .IN(register_2_q[7:0]));
  assign DATA_OUT = or_6_out ? rsh_1_out : 8'bz;  // Controlled_Buffer controlled_buffer_9
  assign COUT = or_6_out ? rsh_1_cout : 1'bz;  // Controlled_Buffer controlled_buffer_10
  assign xor_1_out = register_2_q[7:0] ^ register_2_q[15:8];  // XOR_Gate xor_1, 8 bits wide
  assign DATA_OUT = XOR ? xor_1_out : 8'bz;  // Controlled_Buffer controlled_buffer_11
  assign nand_1_out = ~(register_2_q[7:0] & register_2_q[15:8]);  // NAND_Gate nand_1, 8 bits wide
  assign DATA_OUT = NAND ? nand_1_out : 8'bz;  // Controlled_Buffer controlled_buffer_12
  and and_1 (OE, CLK, ~RW, ENA);  // AND_Gate
  Decoder #(.select(4), .disabled(0)) decoder_1 (
    .out0(ADD), .out1(ADC), .out2(SUB), .out3(SBC), .out4(LSH), .out5(LSC), .out6(RSH), .out7(RSC),
    .out8(XOR), .out9(NAND), .sel(OPCODE), .en(OE));  // open: out10, out11, out12, out13, out14, out15

  // Other names for the same wires on the sheet: CE = ENA

  // Notes on the sheet:
  //   ENA: pull=down
  //   DATA_OUT: pull=down
  //   DATA_IN: pull=down
  //   OPCODE: pull=down
  //   RW: pull=down
  //   CLK: pull=down
endmodule

module LSH (
  input  [7:0] IN,
  input  CIN,
  output COUT,
  output [7:0] OUT
);

  Pull_Resistor pull_resistor_1 (.node(IN[7]));

  assign COUT = IN[7];
  assign OUT = {IN[6:0], CIN};

  // Notes on the sheet:
  //   COUT: pull=down
  //   CIN: pull=down
  //   IN: pull=down
  //   OUT: pull=down
endmodule

module RSH (
  input  CIN,
  input  [7:0] IN,
  output [7:0] OUT,
  output COUT
);

  Pull_Resistor pull_resistor_1 (.node(IN[0]));

  assign COUT = IN[0];
  assign OUT = {CIN, IN[7:1]};

  // Notes on the sheet:
  //   IN: pull=down
  //   OUT: pull=down
  //   COUT: pull=down
  //   CIN: pull=down
endmodule

module REG6_8 (
  input  A_ENA,
  input  C_ENA,
  input  E_ENA,
  input  [3:0] REG_A_ADDR,
  input  [3:0] REG_C_ADDR,
  input  [3:0] REG_E_ADDR,
  input  [31:0] A_IN,
  input  [31:0] C_IN,
  input  [31:0] E_IN,
  input  B_ENA,
  input  D_ENA,
  input  F_ENA,
  input  [3:0] REG_B_ADDR,
  input  [3:0] REG_D_ADDR,
  input  [3:0] REG_F_ADDR,
  input  [31:0] B_IN,
  input  [31:0] D_IN,
  input  [31:0] F_IN,
  input  _0_ENA,
  input  CLK,
  input  WE,
  output [31:0] A_OUT,
  output [31:0] C_OUT,
  output [31:0] E_OUT,
  output [31:0] B_OUT,
  output [31:0] D_OUT,
  output [31:0] F_OUT
);

  wire A_0, A_1, A_2, A_3, A_4, A_5, A_6, A_7, A_8, A_9, A_A, A_B, A_C, A_D, A_E, A_F, B_0, B_1, B_2, B_3,
       B_4, B_5, B_6, B_7, B_8, B_9, B_A, B_B, B_C, B_D, B_E, B_F, C_0, C_1, C_2, C_3, C_4, C_5, C_6, C_7,
       C_8, C_9, C_A, C_B, C_C, C_D, C_E, C_F, D_0, D_1, D_2, D_3, D_4, D_5, D_6, D_7, D_8, D_9, D_A, D_B,
       D_C, D_D, D_E, D_F, E_0, E_1, E_2, E_3, E_4, E_5, E_6, E_7, E_8, E_9, E_A, E_B, E_C, E_D, E_E, E_F,
       F_0, F_1, F_2, F_3, F_4, F_5, F_6, F_7, F_8, F_9, F_A, F_B, F_C, F_D, F_E, F_F;
  wire [2:0] bitfinder_1_index, bitfinder_2_index, bitfinder_3_index, bitfinder_4_index, bitfinder_5_index,
       bitfinder_6_index, bitfinder_7_index, bitfinder_8_index, bitfinder_9_index, bitfinder_10_index,
       bitfinder_11_index, bitfinder_12_index, bitfinder_13_index, bitfinder_14_index, bitfinder_15_index,
       bitfinder_16_index;
  wire [5:0] and_1_out, and_2_out, and_3_out, and_4_out, and_5_out, and_6_out, and_7_out, and_8_out,
       and_9_out, and_10_out, and_11_out, and_12_out, and_13_out, and_14_out, and_15_out, and_16_out;
  wire [31:0] multiplexer_1_out, multiplexer_2_out, multiplexer_3_out, multiplexer_4_out, multiplexer_5_out,
       multiplexer_6_out, multiplexer_7_out, multiplexer_8_out, multiplexer_9_out, multiplexer_10_out,
       multiplexer_11_out, multiplexer_12_out, multiplexer_13_out, multiplexer_14_out, multiplexer_15_out,
       multiplexer_16_out, register_1_q, register_2_q, register_3_q, register_4_q, register_5_q,
       register_6_q, register_7_q, register_8_q, register_9_q, register_10_q, register_11_q, register_12_q,
       register_13_q, register_14_q, register_15_q, register_16_q;

  assign and_1_out = ~{6{WE}} & {F_0, E_0, D_0, C_0, B_0, A_0};  // AND_Gate and_1, 6 bits wide
  assign and_2_out = ~{6{WE}} & {F_1, E_1, D_1, C_1, B_1, A_1};  // AND_Gate and_2, 6 bits wide
  assign and_3_out = ~{6{WE}} & {F_2, E_2, D_2, C_2, B_2, A_2};  // AND_Gate and_3, 6 bits wide
  assign and_4_out = ~{6{WE}} & {F_3, E_3, D_3, C_3, B_3, A_3};  // AND_Gate and_4, 6 bits wide
  BitFinder #(.width(6)) bitfinder_1 (.in({F_0, E_0, D_0, C_0, B_0, A_0}), .index(bitfinder_1_index));  // open: found
  BitFinder #(.width(6)) bitfinder_2 (.in({F_1, E_1, D_1, C_1, B_1, A_1}), .index(bitfinder_2_index));  // open: found
  BitFinder #(.width(6)) bitfinder_3 (.in({F_2, E_2, D_2, C_2, B_2, A_2}), .index(bitfinder_3_index));  // open: found
  BitFinder #(.width(6)) bitfinder_4 (.in({F_3, E_3, D_3, C_3, B_3, A_3}), .index(bitfinder_4_index));  // open: found
  Multiplexer #(.select(3), .width(32), .disabled(0), .enable("false")) multiplexer_1 (
    .in0(A_IN), .in1(B_IN), .in2(C_IN), .in3(D_IN), .in4(E_IN), .in5(F_IN), .out(multiplexer_1_out),
    .sel(bitfinder_1_index));  // open: in6, in7
  Multiplexer #(.select(3), .width(32), .disabled(0), .enable("false")) multiplexer_2 (
    .in0(A_IN), .in1(B_IN), .in2(C_IN), .in3(D_IN), .in4(E_IN), .in5(F_IN), .out(multiplexer_2_out),
    .sel(bitfinder_2_index));  // open: in6, in7
  Multiplexer #(.select(3), .width(32), .disabled(0), .enable("false")) multiplexer_3 (
    .in0(A_IN), .in1(B_IN), .in2(C_IN), .in3(D_IN), .in4(E_IN), .in5(F_IN), .out(multiplexer_3_out),
    .sel(bitfinder_3_index));  // open: in6, in7
  Multiplexer #(.select(3), .width(32), .disabled(0), .enable("false")) multiplexer_4 (
    .in0(A_IN), .in1(B_IN), .in2(C_IN), .in3(D_IN), .in4(E_IN), .in5(F_IN), .out(multiplexer_4_out),
    .sel(bitfinder_4_index));  // open: in6, in7
  Register #(.width(32)) register_1 (.D(multiplexer_1_out), .en(WE), .Q(register_1_q), .clk(CLK), .clr(_0_ENA));
  assign B_OUT = and_1_out[1] ? register_1_q : 32'bz;  // Controlled_Buffer controlled_buffer_1
  assign A_OUT = and_1_out[0] ? register_1_q : 32'bz;  // Controlled_Buffer controlled_buffer_2
  Register #(.width(32)) register_2 (.D(multiplexer_2_out), .en(WE), .Q(register_2_q), .clk(CLK));  // open: clr
  assign B_OUT = and_2_out[1] ? register_2_q : 32'bz;  // Controlled_Buffer controlled_buffer_3
  assign A_OUT = and_2_out[0] ? register_2_q : 32'bz;  // Controlled_Buffer controlled_buffer_4
  Register #(.width(32)) register_3 (.D(multiplexer_3_out), .en(WE), .Q(register_3_q), .clk(CLK));  // open: clr
  assign B_OUT = and_3_out[1] ? register_3_q : 32'bz;  // Controlled_Buffer controlled_buffer_5
  assign A_OUT = and_3_out[0] ? register_3_q : 32'bz;  // Controlled_Buffer controlled_buffer_6
  Register #(.width(32)) register_4 (.D(multiplexer_4_out), .en(WE), .Q(register_4_q), .clk(CLK));  // open: clr
  assign A_OUT = and_4_out[0] ? register_4_q : 32'bz;  // Controlled_Buffer controlled_buffer_7
  assign B_OUT = and_4_out[1] ? register_4_q : 32'bz;  // Controlled_Buffer controlled_buffer_8
  assign C_OUT = and_1_out[2] ? register_1_q : 32'bz;  // Controlled_Buffer controlled_buffer_9
  assign C_OUT = and_2_out[2] ? register_2_q : 32'bz;  // Controlled_Buffer controlled_buffer_10
  assign C_OUT = and_3_out[2] ? register_3_q : 32'bz;  // Controlled_Buffer controlled_buffer_11
  assign C_OUT = and_4_out[2] ? register_4_q : 32'bz;  // Controlled_Buffer controlled_buffer_12
  Decoder #(.select(4), .disabled(0)) decoder_1 (
    .out0(A_0), .out1(A_1), .out2(A_2), .out3(A_3), .out4(A_4), .out5(A_5), .out6(A_6), .out7(A_7),
    .out8(A_8), .out9(A_9), .out10(A_A), .out11(A_B), .out12(A_C), .out13(A_D), .out14(A_E), .out15(A_F),
    .sel(REG_A_ADDR), .en(A_ENA));
  Decoder #(.select(4), .disabled(0)) decoder_2 (
    .out0(B_0), .out1(B_1), .out2(B_2), .out3(B_3), .out4(B_4), .out5(B_5), .out6(B_6), .out7(B_7),
    .out8(B_8), .out9(B_9), .out10(B_A), .out11(B_B), .out12(B_C), .out13(B_D), .out14(B_E), .out15(B_F),
    .sel(REG_B_ADDR), .en(B_ENA));
  assign D_OUT = and_1_out[3] ? register_1_q : 32'bz;  // Controlled_Buffer controlled_buffer_13
  assign E_OUT = and_1_out[4] ? register_1_q : 32'bz;  // Controlled_Buffer controlled_buffer_14
  assign E_OUT = and_2_out[4] ? register_2_q : 32'bz;  // Controlled_Buffer controlled_buffer_15
  assign D_OUT = and_2_out[3] ? register_2_q : 32'bz;  // Controlled_Buffer controlled_buffer_16
  assign D_OUT = and_3_out[3] ? register_3_q : 32'bz;  // Controlled_Buffer controlled_buffer_17
  assign E_OUT = and_3_out[4] ? register_3_q : 32'bz;  // Controlled_Buffer controlled_buffer_18
  assign E_OUT = and_4_out[4] ? register_4_q : 32'bz;  // Controlled_Buffer controlled_buffer_19
  assign D_OUT = and_4_out[3] ? register_4_q : 32'bz;  // Controlled_Buffer controlled_buffer_20
  assign F_OUT = and_1_out[5] ? register_1_q : 32'bz;  // Controlled_Buffer controlled_buffer_21
  assign F_OUT = and_2_out[5] ? register_2_q : 32'bz;  // Controlled_Buffer controlled_buffer_22
  assign F_OUT = and_3_out[5] ? register_3_q : 32'bz;  // Controlled_Buffer controlled_buffer_23
  assign F_OUT = and_4_out[5] ? register_4_q : 32'bz;  // Controlled_Buffer controlled_buffer_24
  assign and_5_out = ~{6{WE}} & {F_4, E_4, D_4, C_4, B_4, A_4};  // AND_Gate and_5, 6 bits wide
  assign and_6_out = ~{6{WE}} & {F_5, E_5, D_5, C_5, B_5, A_5};  // AND_Gate and_6, 6 bits wide
  assign and_7_out = ~{6{WE}} & {F_6, E_6, D_6, C_6, B_6, A_6};  // AND_Gate and_7, 6 bits wide
  assign and_8_out = ~{6{WE}} & {F_7, E_7, D_7, C_7, B_7, A_7};  // AND_Gate and_8, 6 bits wide
  Decoder #(.select(4), .disabled(0)) decoder_3 (
    .out0(C_0), .out1(C_1), .out2(C_2), .out3(C_3), .out4(C_4), .out5(C_5), .out6(C_6), .out7(C_7),
    .out8(C_8), .out9(C_9), .out10(C_A), .out11(C_B), .out12(C_C), .out13(C_D), .out14(C_E), .out15(C_F),
    .sel(REG_C_ADDR), .en(C_ENA));
  Decoder #(.select(4), .disabled(0)) decoder_4 (
    .out0(D_0), .out1(D_1), .out2(D_2), .out3(D_3), .out4(D_4), .out5(D_5), .out6(D_6), .out7(D_7),
    .out8(D_8), .out9(D_9), .out10(D_A), .out11(D_B), .out12(D_C), .out13(D_D), .out14(D_E), .out15(D_F),
    .sel(REG_D_ADDR), .en(D_ENA));
  BitFinder #(.width(6)) bitfinder_5 (.in({F_4, E_4, D_4, C_4, B_4, A_4}), .index(bitfinder_5_index));  // open: found
  Multiplexer #(.select(3), .width(32), .disabled(0), .enable("false")) multiplexer_5 (
    .in0(A_IN), .in1(B_IN), .in2(C_IN), .in3(D_IN), .in4(E_IN), .in5(F_IN), .out(multiplexer_5_out),
    .sel(bitfinder_5_index));  // open: in6, in7
  BitFinder #(.width(6)) bitfinder_6 (.in({F_5, E_5, D_5, C_5, B_5, A_5}), .index(bitfinder_6_index));  // open: found
  Multiplexer #(.select(3), .width(32), .disabled(0), .enable("false")) multiplexer_6 (
    .in0(A_IN), .in1(B_IN), .in2(C_IN), .in3(D_IN), .in4(E_IN), .in5(F_IN), .out(multiplexer_6_out),
    .sel(bitfinder_6_index));  // open: in6, in7
  BitFinder #(.width(6)) bitfinder_7 (.in({F_6, E_6, D_6, C_6, B_6, A_6}), .index(bitfinder_7_index));  // open: found
  Multiplexer #(.select(3), .width(32), .disabled(0), .enable("false")) multiplexer_7 (
    .in0(A_IN), .in1(B_IN), .in2(C_IN), .in3(D_IN), .in4(E_IN), .in5(F_IN), .out(multiplexer_7_out),
    .sel(bitfinder_7_index));  // open: in6, in7
  BitFinder #(.width(6)) bitfinder_8 (.in({F_7, E_7, D_7, C_7, B_7, A_7}), .index(bitfinder_8_index));  // open: found
  Multiplexer #(.select(3), .width(32), .disabled(0), .enable("false")) multiplexer_8 (
    .in0(A_IN), .in1(B_IN), .in2(C_IN), .in3(D_IN), .in4(E_IN), .in5(F_IN), .out(multiplexer_8_out),
    .sel(bitfinder_8_index));  // open: in6, in7
  Decoder #(.select(4), .disabled(0)) decoder_5 (
    .out0(E_0), .out1(E_1), .out2(E_2), .out3(E_3), .out4(E_4), .out5(E_5), .out6(E_6), .out7(E_7),
    .out8(E_8), .out9(E_9), .out10(E_A), .out11(E_B), .out12(E_C), .out13(E_D), .out14(E_E), .out15(E_F),
    .sel(REG_E_ADDR), .en(E_ENA));
  Decoder #(.select(4), .disabled(0)) decoder_6 (
    .out0(F_0), .out1(F_1), .out2(F_2), .out3(F_3), .out4(F_4), .out5(F_5), .out6(F_6), .out7(F_7),
    .out8(F_8), .out9(F_9), .out10(F_A), .out11(F_B), .out12(F_C), .out13(F_D), .out14(F_E), .out15(F_F),
    .sel(REG_F_ADDR), .en(F_ENA));
  Register #(.width(32)) register_5 (.D(multiplexer_5_out), .en(WE), .Q(register_5_q), .clk(CLK), .clr(_0_ENA));
  assign A_OUT = and_5_out[0] ? register_5_q : 32'bz;  // Controlled_Buffer controlled_buffer_25
  Register #(.width(32)) register_6 (.D(multiplexer_6_out), .en(WE), .Q(register_6_q), .clk(CLK));  // open: clr
  assign A_OUT = and_6_out[0] ? register_6_q : 32'bz;  // Controlled_Buffer controlled_buffer_26
  Register #(.width(32)) register_7 (.D(multiplexer_7_out), .en(WE), .Q(register_7_q), .clk(CLK));  // open: clr
  assign A_OUT = and_7_out[0] ? register_7_q : 32'bz;  // Controlled_Buffer controlled_buffer_27
  Register #(.width(32)) register_8 (.D(multiplexer_8_out), .en(WE), .Q(register_8_q), .clk(CLK));  // open: clr
  assign A_OUT = and_8_out[0] ? register_8_q : 32'bz;  // Controlled_Buffer controlled_buffer_28
  assign C_OUT = and_5_out[2] ? register_5_q : 32'bz;  // Controlled_Buffer controlled_buffer_29
  assign B_OUT = and_5_out[1] ? register_5_q : 32'bz;  // Controlled_Buffer controlled_buffer_30
  assign B_OUT = and_6_out[1] ? register_6_q : 32'bz;  // Controlled_Buffer controlled_buffer_31
  assign C_OUT = and_6_out[2] ? register_6_q : 32'bz;  // Controlled_Buffer controlled_buffer_32
  assign C_OUT = and_7_out[2] ? register_7_q : 32'bz;  // Controlled_Buffer controlled_buffer_33
  assign B_OUT = and_7_out[1] ? register_7_q : 32'bz;  // Controlled_Buffer controlled_buffer_34
  assign C_OUT = and_8_out[2] ? register_8_q : 32'bz;  // Controlled_Buffer controlled_buffer_35
  assign B_OUT = and_8_out[1] ? register_8_q : 32'bz;  // Controlled_Buffer controlled_buffer_36
  assign D_OUT = and_5_out[3] ? register_5_q : 32'bz;  // Controlled_Buffer controlled_buffer_37
  assign D_OUT = and_6_out[3] ? register_6_q : 32'bz;  // Controlled_Buffer controlled_buffer_38
  assign D_OUT = and_7_out[3] ? register_7_q : 32'bz;  // Controlled_Buffer controlled_buffer_39
  assign D_OUT = and_8_out[3] ? register_8_q : 32'bz;  // Controlled_Buffer controlled_buffer_40
  assign E_OUT = and_5_out[4] ? register_5_q : 32'bz;  // Controlled_Buffer controlled_buffer_41
  assign F_OUT = and_5_out[5] ? register_5_q : 32'bz;  // Controlled_Buffer controlled_buffer_42
  assign F_OUT = and_6_out[5] ? register_6_q : 32'bz;  // Controlled_Buffer controlled_buffer_43
  assign E_OUT = and_6_out[4] ? register_6_q : 32'bz;  // Controlled_Buffer controlled_buffer_44
  assign F_OUT = and_7_out[5] ? register_7_q : 32'bz;  // Controlled_Buffer controlled_buffer_45
  assign E_OUT = and_7_out[4] ? register_7_q : 32'bz;  // Controlled_Buffer controlled_buffer_46
  assign E_OUT = and_8_out[4] ? register_8_q : 32'bz;  // Controlled_Buffer controlled_buffer_47
  assign F_OUT = and_8_out[5] ? register_8_q : 32'bz;  // Controlled_Buffer controlled_buffer_48
  assign and_9_out = ~{6{WE}} & {F_8, E_8, D_8, C_8, B_8, A_8};  // AND_Gate and_9, 6 bits wide
  assign and_10_out = ~{6{WE}} & {F_9, E_9, D_9, C_9, B_9, A_9};  // AND_Gate and_10, 6 bits wide
  assign and_11_out = ~{6{WE}} & {F_A, E_A, D_A, C_A, B_A, A_A};  // AND_Gate and_11, 6 bits wide
  assign and_12_out = ~{6{WE}} & {F_B, E_B, D_B, C_B, B_B, A_B};  // AND_Gate and_12, 6 bits wide
  BitFinder #(.width(6)) bitfinder_9 (.in({F_8, E_8, D_8, C_8, B_8, A_8}), .index(bitfinder_9_index));  // open: found
  BitFinder #(.width(6)) bitfinder_10 (.in({F_9, E_9, D_9, C_9, B_9, A_9}), .index(bitfinder_10_index));  // open: found
  BitFinder #(.width(6)) bitfinder_11 (.in({F_A, E_A, D_A, C_A, B_A, A_A}), .index(bitfinder_11_index));  // open: found
  BitFinder #(.width(6)) bitfinder_12 (.in({F_B, E_B, D_B, C_B, B_B, A_B}), .index(bitfinder_12_index));  // open: found
  Multiplexer #(.select(3), .width(32), .disabled(0), .enable("false")) multiplexer_9 (
    .in0(A_IN), .in1(B_IN), .in2(C_IN), .in3(D_IN), .in4(E_IN), .in5(F_IN), .out(multiplexer_9_out),
    .sel(bitfinder_9_index));  // open: in6, in7
  Register #(.width(32)) register_9 (.D(multiplexer_9_out), .en(WE), .Q(register_9_q), .clk(CLK), .clr(_0_ENA));
  Register #(.width(32)) register_10 (.D(multiplexer_10_out), .en(WE), .Q(register_10_q), .clk(CLK));  // open: clr
  Multiplexer #(.select(3), .width(32), .disabled(0), .enable("false")) multiplexer_10 (
    .in0(A_IN), .in1(B_IN), .in2(C_IN), .in3(D_IN), .in4(E_IN), .in5(F_IN), .out(multiplexer_10_out),
    .sel(bitfinder_10_index));  // open: in6, in7
  Register #(.width(32)) register_11 (.D(multiplexer_11_out), .en(WE), .Q(register_11_q), .clk(CLK));  // open: clr
  Multiplexer #(.select(3), .width(32), .disabled(0), .enable("false")) multiplexer_11 (
    .in0(A_IN), .in1(B_IN), .in2(C_IN), .in3(D_IN), .in4(E_IN), .in5(F_IN), .out(multiplexer_11_out),
    .sel(bitfinder_11_index));  // open: in6, in7
  Register #(.width(32)) register_12 (.D(multiplexer_12_out), .en(WE), .Q(register_12_q), .clk(CLK));  // open: clr
  Multiplexer #(.select(3), .width(32), .disabled(0), .enable("false")) multiplexer_12 (
    .in0(A_IN), .in1(B_IN), .in2(C_IN), .in3(D_IN), .in4(E_IN), .in5(F_IN), .out(multiplexer_12_out),
    .sel(bitfinder_12_index));  // open: in6, in7
  assign A_OUT = and_9_out[0] ? register_9_q : 32'bz;  // Controlled_Buffer controlled_buffer_49
  assign B_OUT = and_9_out[1] ? register_9_q : 32'bz;  // Controlled_Buffer controlled_buffer_50
  assign A_OUT = and_10_out[0] ? register_10_q : 32'bz;  // Controlled_Buffer controlled_buffer_51
  assign B_OUT = and_10_out[1] ? register_10_q : 32'bz;  // Controlled_Buffer controlled_buffer_52
  assign A_OUT = and_11_out[0] ? register_11_q : 32'bz;  // Controlled_Buffer controlled_buffer_53
  assign B_OUT = and_11_out[1] ? register_11_q : 32'bz;  // Controlled_Buffer controlled_buffer_54
  assign A_OUT = and_12_out[0] ? register_12_q : 32'bz;  // Controlled_Buffer controlled_buffer_55
  assign B_OUT = and_12_out[1] ? register_12_q : 32'bz;  // Controlled_Buffer controlled_buffer_56
  assign C_OUT = and_9_out[2] ? register_9_q : 32'bz;  // Controlled_Buffer controlled_buffer_57
  assign C_OUT = and_10_out[2] ? register_10_q : 32'bz;  // Controlled_Buffer controlled_buffer_58
  assign C_OUT = and_11_out[2] ? register_11_q : 32'bz;  // Controlled_Buffer controlled_buffer_59
  assign C_OUT = and_12_out[2] ? register_12_q : 32'bz;  // Controlled_Buffer controlled_buffer_60
  assign D_OUT = and_9_out[3] ? register_9_q : 32'bz;  // Controlled_Buffer controlled_buffer_61
  assign E_OUT = and_9_out[4] ? register_9_q : 32'bz;  // Controlled_Buffer controlled_buffer_62
  assign D_OUT = and_10_out[3] ? register_10_q : 32'bz;  // Controlled_Buffer controlled_buffer_63
  assign E_OUT = and_10_out[4] ? register_10_q : 32'bz;  // Controlled_Buffer controlled_buffer_64
  assign D_OUT = and_11_out[3] ? register_11_q : 32'bz;  // Controlled_Buffer controlled_buffer_65
  assign E_OUT = and_11_out[4] ? register_11_q : 32'bz;  // Controlled_Buffer controlled_buffer_66
  assign D_OUT = and_12_out[3] ? register_12_q : 32'bz;  // Controlled_Buffer controlled_buffer_67
  assign E_OUT = and_12_out[4] ? register_12_q : 32'bz;  // Controlled_Buffer controlled_buffer_68
  assign F_OUT = and_9_out[5] ? register_9_q : 32'bz;  // Controlled_Buffer controlled_buffer_69
  assign F_OUT = and_10_out[5] ? register_10_q : 32'bz;  // Controlled_Buffer controlled_buffer_70
  assign F_OUT = and_11_out[5] ? register_11_q : 32'bz;  // Controlled_Buffer controlled_buffer_71
  assign F_OUT = and_12_out[5] ? register_12_q : 32'bz;  // Controlled_Buffer controlled_buffer_72
  assign and_13_out = ~{6{WE}} & {F_C, E_C, D_C, C_C, B_C, A_C};  // AND_Gate and_13, 6 bits wide
  assign and_14_out = ~{6{WE}} & {F_D, E_D, D_D, C_D, B_D, A_D};  // AND_Gate and_14, 6 bits wide
  assign and_15_out = ~{6{WE}} & {F_E, E_E, D_E, C_E, B_E, A_E};  // AND_Gate and_15, 6 bits wide
  assign and_16_out = ~{6{WE}} & {F_F, E_F, D_F, C_F, B_F, A_F};  // AND_Gate and_16, 6 bits wide
  BitFinder #(.width(6)) bitfinder_13 (.in({F_C, E_C, D_C, C_C, B_C, A_C}), .index(bitfinder_13_index));  // open: found
  Multiplexer #(.select(3), .width(32), .disabled(0), .enable("false")) multiplexer_13 (
    .in0(A_IN), .in1(B_IN), .in2(C_IN), .in3(D_IN), .in4(E_IN), .in5(F_IN), .out(multiplexer_13_out),
    .sel(bitfinder_13_index));  // open: in6, in7
  BitFinder #(.width(6)) bitfinder_14 (.in({F_D, E_D, D_D, C_D, B_D, A_D}), .index(bitfinder_14_index));  // open: found
  Multiplexer #(.select(3), .width(32), .disabled(0), .enable("false")) multiplexer_14 (
    .in0(A_IN), .in1(B_IN), .in2(C_IN), .in3(D_IN), .in4(E_IN), .in5(F_IN), .out(multiplexer_14_out),
    .sel(bitfinder_14_index));  // open: in6, in7
  BitFinder #(.width(6)) bitfinder_15 (.in({F_E, E_E, D_E, C_E, B_E, A_E}), .index(bitfinder_15_index));  // open: found
  Multiplexer #(.select(3), .width(32), .disabled(0), .enable("false")) multiplexer_15 (
    .in0(A_IN), .in1(B_IN), .in2(C_IN), .in3(D_IN), .in4(E_IN), .in5(F_IN), .out(multiplexer_15_out),
    .sel(bitfinder_15_index));  // open: in6, in7
  BitFinder #(.width(6)) bitfinder_16 (.in({F_F, E_F, D_F, C_F, B_F, A_F}), .index(bitfinder_16_index));  // open: found
  Multiplexer #(.select(3), .width(32), .disabled(0), .enable("false")) multiplexer_16 (
    .in0(A_IN), .in1(B_IN), .in2(C_IN), .in3(D_IN), .in4(E_IN), .in5(F_IN), .out(multiplexer_16_out),
    .sel(bitfinder_16_index));  // open: in6, in7
  Register #(.width(32)) register_13 (.D(multiplexer_13_out), .en(WE), .Q(register_13_q), .clk(CLK), .clr(_0_ENA));
  assign A_OUT = and_13_out[0] ? register_13_q : 32'bz;  // Controlled_Buffer controlled_buffer_73
  Register #(.width(32)) register_14 (.D(multiplexer_14_out), .en(WE), .Q(register_14_q), .clk(CLK));  // open: clr
  assign A_OUT = and_14_out[0] ? register_14_q : 32'bz;  // Controlled_Buffer controlled_buffer_74
  Register #(.width(32)) register_15 (.D(multiplexer_15_out), .en(WE), .Q(register_15_q), .clk(CLK));  // open: clr
  assign A_OUT = and_15_out[0] ? register_15_q : 32'bz;  // Controlled_Buffer controlled_buffer_75
  Register #(.width(32)) register_16 (.D(multiplexer_16_out), .en(WE), .Q(register_16_q), .clk(CLK));  // open: clr
  assign A_OUT = and_16_out[0] ? register_16_q : 32'bz;  // Controlled_Buffer controlled_buffer_76
  assign C_OUT = and_13_out[2] ? register_13_q : 32'bz;  // Controlled_Buffer controlled_buffer_77
  assign B_OUT = and_13_out[1] ? register_13_q : 32'bz;  // Controlled_Buffer controlled_buffer_78
  assign C_OUT = and_14_out[2] ? register_14_q : 32'bz;  // Controlled_Buffer controlled_buffer_79
  assign B_OUT = and_14_out[1] ? register_14_q : 32'bz;  // Controlled_Buffer controlled_buffer_80
  assign C_OUT = and_15_out[2] ? register_15_q : 32'bz;  // Controlled_Buffer controlled_buffer_81
  assign B_OUT = and_15_out[1] ? register_15_q : 32'bz;  // Controlled_Buffer controlled_buffer_82
  assign C_OUT = and_16_out[2] ? register_16_q : 32'bz;  // Controlled_Buffer controlled_buffer_83
  assign B_OUT = and_16_out[1] ? register_16_q : 32'bz;  // Controlled_Buffer controlled_buffer_84
  assign E_OUT = and_13_out[4] ? register_13_q : 32'bz;  // Controlled_Buffer controlled_buffer_85
  assign D_OUT = and_13_out[3] ? register_13_q : 32'bz;  // Controlled_Buffer controlled_buffer_86
  assign D_OUT = and_14_out[3] ? register_14_q : 32'bz;  // Controlled_Buffer controlled_buffer_87
  assign E_OUT = and_14_out[4] ? register_14_q : 32'bz;  // Controlled_Buffer controlled_buffer_88
  assign D_OUT = and_15_out[3] ? register_15_q : 32'bz;  // Controlled_Buffer controlled_buffer_89
  assign E_OUT = and_15_out[4] ? register_15_q : 32'bz;  // Controlled_Buffer controlled_buffer_90
  assign D_OUT = and_16_out[3] ? register_16_q : 32'bz;  // Controlled_Buffer controlled_buffer_91
  assign E_OUT = and_16_out[4] ? register_16_q : 32'bz;  // Controlled_Buffer controlled_buffer_92
  assign F_OUT = and_13_out[5] ? register_13_q : 32'bz;  // Controlled_Buffer controlled_buffer_93
  assign F_OUT = and_14_out[5] ? register_14_q : 32'bz;  // Controlled_Buffer controlled_buffer_94
  assign F_OUT = and_15_out[5] ? register_15_q : 32'bz;  // Controlled_Buffer controlled_buffer_95
  assign F_OUT = and_16_out[5] ? register_16_q : 32'bz;  // Controlled_Buffer controlled_buffer_96

  // Notes on the sheet:
  //   CLK: pull=down
  //   REG_F_ADDR: pull=down
  //   REG_D_ADDR: pull=down
  //   REG_C_ADDR: pull=down
  //   C_ENA: pull=down
  //   A_ENA: pull=down
  //   F_ENA: pull=down
  //   B_OUT: pull=down
  //   REG_A_ADDR: pull=down
  //   WE: pull=down
  //   REG_E_ADDR: pull=down
  //   D_OUT: pull=down
  //   D_ENA: pull=down
  //   E_OUT: pull=down
  //   E_ENA: pull=down
  //   REG_B_ADDR: pull=down
  //   A_OUT: pull=down
  //   B_ENA: pull=down
  //   _0_ENA: pull=down
  //   C_OUT: pull=down
  //   F_OUT: pull=down
endmodule
